# Fritzing sketch Fhotibot2_Head (saved by Fritzing 0.7.0b)
breadboards: 1

parts:
  Nano1 = Arduino Nano v2.3
  Back = Photocell (LDR) [package=THT]
  Front = Photocell (LDR) [package=THT]
  R3 = Resistor [tolerance=±5% resistance=10k package=THT]
  R4 = Resistor [tolerance=±5% resistance=10k package=THT]
  LED1 = LED - 5mm [color="Red (633nm)" package="5 mm [THT]"]
  Vertical = Basic Servo
  Horizontal = Basic Servo
  LED2 = LED - 5mm [color="Green (555nm)" package="5 mm [THT]"]
  LED3 = LED - 5mm [color="Yellow (585nm)" package="5 mm [THT]"]
  ANT1 = Antenna
  Front_2 = Microphone
  Right = Microphone
  Left = Microphone

nets:
  GND: Nano1.GND, R3.Pin_1, R4.Pin_1, LED1.cathode, Vertical.gnd, Horizontal.gnd, LED2.cathode, LED3.cathode
  N1: Nano1.D2, LED1.anode
  N2: Nano1.D3, LED2.anode
  N3: Nano1.D4, LED3.anode
  N4: Nano1.D10, Horizontal.pulse
  N5: Nano1.D11, Vertical.pulse
  N6: Nano1.A7, ANT1.antenna_lead
  N7: Nano1.A5, Right.pin1
  N8: Nano1.A4, Front_2.pin1
  N9: Nano1.A3, Left.pin1
  N10: Nano1.A1, Front.pin_0, R3.Pin_0
  N11: Nano1.A0, Back.pin_0, R4.Pin_0
  VCC: Nano1.+5V, Back.pin_1, Front.pin_1, Vertical.vcc, Horizontal.vcc, Front_2.pin2, Right.pin2, Left.pin2
